// Digital circuit controlUnit.dig as structural Verilog
module controlUnit (
  input  [31:0] A,
  input  zero,
  output [12:0] out
);

  wire and_1_out;
  wire [1:0] OPcode_commander_d;
  wire [2:0] ULA_commander_d;

  ROM #(.AddrBits(7), .Bits(11)) OPcode_commander (.A(A[6:0]), .sel(1'b1), .D({out[9], out[7:0], OPcode_commander_d}));
  ROM #(.AddrBits(10), .Bits(3)) ULA_commander (.A({A[31:25], A[14:12]}), .sel(1'b1), .D(ULA_commander_d));
  and and_1 (and_1_out, zero, OPcode_commander_d[1]);
  Multiplexer #(.Bits(3)) multiplexer_1 (.sel(A[4]), .in_0(3'b000), .in_1(ULA_commander_d), .out(out[12:10]));
  or or_1 (out[8], and_1_out, OPcode_commander_d[0]);

  // Other names for the same wires on the sheet: OP_code[6:0] = A[6:0]

  // Notes on the sheet:
  //   contents of OPcode_commander (hex, n*v repeats v):
  //   0,0,254,16*0,19,19,18*0,48,17*0,200
  //   contents of ULA_commander (hex, n*v repeats v):
  //   0,5,1,0,3,0,4,2,0,0,0,1
endmodule
