// Digital circuit immediateTransformer.dig as structural Verilog
module immediateTransformer (
  input  [1:0] ImmC,
  input  [31:0] in,
  output [31:0] \output 
);

  wire [31:0] B_type, I_type, J_type, S_type;

  BitExtender #(.inputBits(12), .outputBits(32)) bitextender_1 (.in(in[31:20]), .out(I_type));
  BitExtender #(.inputBits(12), .outputBits(32)) bitextender_2 (.in({in[31:25], in[11:7]}), .out(S_type));
  BitExtender #(.inputBits(13), .outputBits(32)) bitextender_3 (
    .in({in[31], in[7], in[30:25], in[11:8], 1'b0}), .out(B_type));
  BitExtender #(.inputBits(21), .outputBits(32)) bitextender_4 (
    .in({in[31], in[19:12], in[20], in[30:21], 1'b0}), .out(J_type));
  Multiplexer #(.Selector_Bits(2), .Bits(32)) multiplexer_1 (
    .sel(ImmC), .in_0(I_type), .in_1(S_type), .in_2(B_type), .in_3(J_type), .out(\output ));

  // Other names for the same wires on the sheet: _0 = in[0]; _1 = in[1]; _2 = in[2]; _3 = in[3]; _4 = in[4];
  //   _5 = in[5]; _6 = in[6]; _7 = in[7]; _8 = in[8]; _9 = in[9]; _10 = in[10]; _11 = in[11]; _12 = in[12];
  //   _13 = in[13]; _14 = in[14]; _15 = in[15]; _16 = in[16]; _17 = in[17]; _18 = in[18]; _19 = in[19]; _20 = in[20];
  //   _21 = in[21]; _22 = in[22]; _23 = in[23]; _24 = in[24]; _25 = in[25]; _26 = in[26]; _27 = in[27]; _28 = in[28];
  //   _29 = in[29]; _30 = in[30]; _31 = in[31]
endmodule
