// Digital circuit registrador.dig as structural Verilog
module registrador (
  input  [31:0] A_2,
  input  [4:0] B_2,
  input  [4:0] C_rd,
  input  [31:0] C_ula,
  input  clk,
  input  W1,
  output [31:0] A,
  output [31:0] B
);

  wire and_1_out, C1, C2, C3, C4, C5;
  wire [4:0] A_t;
  wire [31:0] f0, f1, f2, f3, f4, f5, f6, f7, f8, f9, f10, f11, f12, f13, f14, f15, f16, f17, f18, f19, f20,
       f21, f22, f23, f24, f25, f26, f27, f28, f29, f30, f31;

  and and_1 (and_1_out, W1, clk);
  Demultiplexer #(.Selector_Bits(5)) demultiplexer_1 (
    .sel(C_rd), .in(and_1_out));  // open: out_0, out_1, out_2, out_3, out_4, out_5, out_6, out_7, out_8, out_9, out_10, out_11, out_12, out_13, out_14, out_15, out_16, out_17, out_18, out_19, out_20, out_21, out_22, out_23, out_24, out_25, out_26, out_27, out_28, out_29, out_30, out_31
  D_FF #(.Bits(32)) _0 (.D(A_2), .C(A_2[0]), .Q(f0));  // open: nQ
  D_FF #(.Bits(32)) _1 (.D(A_2), .C(C1), .Q(f1));  // open: nQ
  D_FF #(.Bits(32)) _2 (.D(A_2), .C(C2), .Q(f2));  // open: nQ
  D_FF #(.Bits(32)) _3 (.D(A_2), .C(C3), .Q(f3));  // open: nQ
  D_FF #(.Bits(32)) _4 (.D(A_2), .C(C4), .Q(f4));  // open: nQ
  D_FF #(.Bits(32)) _5 (.D(A_2), .C(C5), .Q(f5));  // open: nQ
  D_FF #(.Bits(32)) _6 (.D(A_2), .C(A_2[0]), .Q(f6));  // open: nQ
  D_FF #(.Bits(32)) _7 (.D(A_2), .C(A_2[0]), .Q(f7));  // open: nQ
  D_FF #(.Bits(32)) _8 (.D(A_2), .C(A_2[0]), .Q(f8));  // open: nQ
  D_FF #(.Bits(32)) _9 (.D(A_2), .C(A_2[0]), .Q(f9));  // open: nQ
  D_FF #(.Bits(32)) _10 (.D(A_2), .C(A_2[0]), .Q(f10));  // open: nQ
  D_FF #(.Bits(32)) _11 (.D(A_2), .C(A_2[0]), .Q(f11));  // open: nQ
  D_FF #(.Bits(32)) _12 (.D(A_2), .C(A_2[0]), .Q(f12));  // open: nQ
  D_FF #(.Bits(32)) _13 (.D(A_2), .C(A_2[0]), .Q(f13));  // open: nQ
  D_FF #(.Bits(32)) _14 (.D(A_2), .C(A_2[0]), .Q(f14));  // open: nQ
  D_FF #(.Bits(32)) _15 (.D(A_2), .C(A_2[0]), .Q(f15));  // open: nQ
  D_FF #(.Bits(32)) _16 (.D(A_2), .C(A_2[0]), .Q(f16));  // open: nQ
  D_FF #(.Bits(32)) _17 (.D(A_2), .C(A_2[0]), .Q(f17));  // open: nQ
  D_FF #(.Bits(32)) _18 (.D(A_2), .C(A_2[0]), .Q(f18));  // open: nQ
  D_FF #(.Bits(32)) _19 (.D(A_2), .C(A_2[0]), .Q(f19));  // open: nQ
  D_FF #(.Bits(32)) _20 (.D(A_2), .C(A_2[0]), .Q(f20));  // open: nQ
  D_FF #(.Bits(32)) _21 (.D(A_2), .C(A_2[0]), .Q(f21));  // open: nQ
  D_FF #(.Bits(32)) _22 (.D(A_2), .C(A_2[0]), .Q(f22));  // open: nQ
  D_FF #(.Bits(32)) _23 (.D(A_2), .C(A_2[0]), .Q(f23));  // open: nQ
  D_FF #(.Bits(32)) _24 (.D(A_2), .C(A_2[0]), .Q(f24));  // open: nQ
  D_FF #(.Bits(32)) _25 (.D(A_2), .C(A_2[0]), .Q(f25));  // open: nQ
  D_FF #(.Bits(32)) _26 (.D(A_2), .C(A_2[0]), .Q(f26));  // open: nQ
  D_FF #(.Bits(32)) _27 (.D(A_2), .C(A_2[0]), .Q(f27));  // open: nQ
  D_FF #(.Bits(32)) _28 (.D(A_2), .C(A_2[0]), .Q(f28));  // open: nQ
  D_FF #(.Bits(32)) _29 (.D(A_2), .C(A_2[0]), .Q(f29));  // open: nQ
  D_FF #(.Bits(32)) _30 (.D(A_2), .C(A_2[0]), .Q(f30));  // open: nQ
  D_FF #(.Bits(32)) _31 (.D(A_2), .C(A_2[0]), .Q(f31));  // open: nQ
  Multiplexer #(.Selector_Bits(5), .Bits(32)) multiplexer_1 (
    .sel(A_t), .in_0(f0), .in_1(f1), .in_2(f2), .in_3(f3), .in_4(f4), .in_5(f5), .in_6(f6), .in_7(f7),
    .in_8(f8), .in_9(f9), .in_10(f10), .in_11(f11), .in_12(f12), .in_13(f13), .in_14(f14), .in_15(f15),
    .in_16(f16), .in_17(f17), .in_18(f18), .in_19(f19), .in_20(f20), .in_21(f21), .in_22(f22), .in_23(f23),
    .in_24(f24), .in_25(f25), .in_26(f26), .in_27(f27), .in_28(f28), .in_29(f29), .in_30(f30), .in_31(f31),
    .out(A));
  Multiplexer #(.Selector_Bits(5), .Bits(32)) multiplexer_2 (
    .sel(B_2), .in_0(f0), .in_1(f1), .in_2(f2), .in_3(f3), .in_4(f4), .in_5(f5), .in_6(f6), .in_7(f7),
    .in_8(f8), .in_9(f9), .in_10(f10), .in_11(f11), .in_12(f12), .in_13(f13), .in_14(f14), .in_15(f15),
    .in_16(f16), .in_17(f17), .in_18(f18), .in_19(f19), .in_20(f20), .in_21(f21), .in_22(f22), .in_23(f23),
    .in_24(f24), .in_25(f25), .in_26(f26), .in_27(f27), .in_28(f28), .in_29(f29), .in_30(f30), .in_31(f31),
    .out(B));
  // Pins of 1 and 5 and 32 bits meet at A_2

  assign C_ula = A_2;

  // Other names for the same wires on the sheet: B_t[4:0] = B_2; Crd[4:0] = C_rd; C0[31:0] = A_2; Cula[31:0] = A_2
endmodule
