// Digital circuit ula.dig as structural Verilog
module ula (
  input  [31:0] A,
  input  [31:0] B,
  input  [2:0] c_ula,
  output [31:0] Output,
  output zero,
  output eq,
  output lt
);

  wire Comparador_lt;
  wire [0:0] Sub_s_2;
  wire [30:0] Sub_s;
  wire [31:0] and_1_out, bitextender_1_out, bitextender_2_out, or_1_out, Shift_Left_out, Sum_s, xor_1_out;

  Add #(.Bits(32)) Sum (.a(A), .b(B), .c_i(1'b0), .s(Sum_s));  // open: c_o
  Sub #(.Bits(32)) Sub (.a(A), .b(B), .c_i(1'b0), .s({Sub_s_2[0], Sub_s}));  // open: c_o
  assign and_1_out = A & B;  // And and_1, 32 bits wide
  assign xor_1_out = A ^ B;  // XOr xor_1, 32 bits wide
  assign or_1_out = A | B;  // Or or_1, 32 bits wide
  BarrelShifter #(.Bits(32), .barrelSigned("true")) Shift_Left (.in(A), .shift(B[6:0]), .out(Shift_Left_out));
  Comparator #(.Signed("true"), .Bits(32)) Comparador (.a(A), .b(B), .lt(Comparador_lt));  // open: gt, eq
  BitExtender #(.inputBits(1), .outputBits(32)) bitextender_1 (.in(Comparador_lt), .out(bitextender_1_out));
  Multiplexer #(.Selector_Bits(3), .Bits(32)) multiplexer_1 (
    .sel(c_ula), .in_0(Sum_s), .in_1({Sub_s_2[0], Sub_s}), .in_2(and_1_out), .in_3(xor_1_out),
    .in_4(or_1_out), .in_5(Shift_Left_out), .in_6({{31{1'b0}}, Sub_s_2[0]}), .in_7(bitextender_1_out),
    .out(Output));
  BitExtender #(.inputBits(1), .outputBits(32)) bitextender_2 (.in(1'b0), .out(bitextender_2_out));
  Comparator #(.Bits(32)) comparator_1 (.a(bitextender_2_out), .b(Output), .eq(zero));  // open: gt, lt
  Comparator #(.Bits(32)) comparator_2 (.a(A), .b(B), .eq(eq), .lt(lt));  // open: gt
endmodule
